# Fritzing sketch tuerklingel (saved by Fritzing 0.9.9b)
circuit board: 2.7806cm x 3.29167cm
perfboards: 1

parts:
  Opto = TLP621 [package=THT]
  R2 = Resistor [tolerance=±5% power=0.25 resistance=1.2k package=THT]
  R3 = Resistor [tolerance=±5% power=0.25 resistance=47k package=THT]
  C2 = Ceramic Capacitor [capacitance=10nF voltage=16V package="100 mil [THT, multilayer]"]
  R1 = Resistor [tolerance=±5% power=0.25 resistance=220 package=THT]
  D1 = Rectifier Diode [part_number=1N4001 package="300 mil [THT]"]
  C1 = Electrolytic Capacitor [capacitance=10μF voltage=16V package="100 mil [THT, electrolytic]"]
  V2 = AC Power [voltage=12V frequency=50]
  V3 = DC Power [voltage=5]
  R4 = Resistor [tolerance=±5% power=0.25 resistance=100k package=THT]
  R5 = Resistor [tolerance=±5% power=0.25 resistance=3k package=THT]
  Main_Header = female pin header, 8 pins [form="♀ (female)"]
  WeMos_D1_Mini_Protoboard_Shield2 = WeMos D1 Mini Protoboard Shield

nets:
  N1: Opto.Pin_1, R2.Pin_1
  12V_AC_N: Opto.Pin_2, R3.Pin_0, C1.-, V2.V-, Main_Header.pin3
  N2: Opto.Pin_4, R5.Pin_1
  Opto_in: Opto.Pin_3, C2.1, R4.Pin_0, WeMos_D1_Mini_Protoboard_Shield2.D6
  N3: R2.Pin_0, R3.Pin_1, D1.cathode, C1.+
  GND: C2.0, V3.V-, R4.Pin_1, Main_Header.pin4, WeMos_D1_Mini_Protoboard_Shield2.G, WeMos_D1_Mini_Protoboard_Shield2.X7-Y7
  12V_AC_L/Gong_In: R1.Pin_0, V2.V+, Main_Header.pin5, Main_Header.pin6
  N4: R1.Pin_1, D1.anode
  5V/5V_DC: V3.V+, Main_Header.pin7, WeMos_D1_Mini_Protoboard_Shield2.5V, WeMos_D1_Mini_Protoboard_Shield2.X7-Y8
  3V3_DC: R5.Pin_0, WeMos_D1_Mini_Protoboard_Shield2.3V3
  Gong_Out/Relay_In: Main_Header.pin1, Main_Header.pin2
  R_Control: Main_Header.pin8, WeMos_D1_Mini_Protoboard_Shield2.TX, WeMos_D1_Mini_Protoboard_Shield2.X7-Y1

notes:
  1 - Relay in
  2 - GND
  3 - VCC (5V)
  Türklingel, Smartifizieren unserer Türklingel (5V DC sind hingelegt, Trafo arbeitet mit ~12V),    1.0
