# Fritzing sketch tuerklingel_komplett (saved by Fritzing 0.9.6b)
perfboards: 1

parts:
  D1 = Rectifier Diode [part_number=1N4001 package="300 mil [THT]"]
  Opto = TLP621 [package=THT]
  R2 = Resistor [tolerance=±5% power=0.25 resistance=1.2k package=THT]
  Klingel-Taster = Round Pushbutton
  R3 = Resistor [tolerance=±5% power=0.25 resistance=47k package=THT]
  R4 = Resistor [tolerance=±5% resistance=100k package="0402 [SMD]"]
  WeMos_D1_Mini1 = WeMos D1 Mini
  R5 = Resistor [tolerance=±5% resistance=3k package="0402 [SMD]"]
  C2 = Ceramic Capacitor [capacitance=10nF voltage=16V package="100 mil [THT, multilayer]"]
  C1 = Electrolytic Capacitor [capacitance=10μF voltage=16V package="200 mil [THT, electrolytic]"]
  Klingeltrafo = AC Power [voltage=12V frequency=50Hz]
  Q1 = MOSFET-NCHANNEL [package=to220v]
  R6 = Resistor [tolerance=±5% power=0.25 resistance=220 package=THT]
  Gong = Header 2 [package=jst-2-pth-kit]
  R1 = Resistor [tolerance=±5% power=0.25 resistance=220 package=THT]
  D2 = Schottky Diode [part_number=1N5817 package="Melf DO-213 AB [SMD]"]
  R7 = Resistor [tolerance=±5% power=0.25 resistance=100k package=THT]
  U1 = RELAY [package=relay-jzc]

nets:
  N1: D1.cathode, R2.Pin_0, R3.Pin_1, C1.+
  N2: D1.anode, R1.Pin_1
  N3: Opto.Pin_1, R2.Pin_1
  N4: Opto.Pin_2, R3.Pin_0, C1.-, Klingeltrafo.V-, Gong.2
  N5: Opto.Pin_4, R5.Pin_1
  Opto_in: Opto.Pin_3, R4.Pin_0, WeMos_D1_Mini1.D1, C2.1
  N6: Klingel-Taster.leg0, Klingeltrafo.V+
  Gong1: Klingel-Taster.leg1, R1.Pin_0, U1.NC
  GND: R4.Pin_1, WeMos_D1_Mini1.G, C2.0, D2.anode, U1.COIL2
  N7: WeMos_D1_Mini1.3V3, R5.Pin_0
  5V: WeMos_D1_Mini1.5V, R6.Pin_1
  Gong_out: WeMos_D1_Mini1.D3, R7.Pin_0
  N8: Q1.G, R7.Pin_1
  N9: Q1.D, D2.cathode, U1.COIL1
  N10: Q1.S, R6.Pin_0
  Gong2: Gong.1, U1.NO, U1.MAIN

notes:
  Wenn Spannungslos,
  Relais aktiv => Gong aktiv!
